// Logisim project milestone_1.circ as structural Verilog
module ALU_control (
  input  I30,
  input  I14,
  input  I13,
  input  I12,
  input  I6,
  input  I5,
  input  I4,
  output ALU_Ctrl3,
  output ALU_Ctrl2,
  output ALU_Ctrl1,
  output ALU_Ctrl0,
  output ALU_Src
);

  wire and_2_out, not_1_out, not_2_out, not_3_out, not_4_out, not_5_out;

  not not_1 (not_1_out, I14);
  not not_2 (not_2_out, I13);
  not not_3 (not_3_out, I12);
  not not_4 (not_4_out, I5);
  not not_5 (not_5_out, I4);
  and and_1 (ALU_Ctrl2, I30, not_2_out, I5);
  or or_1 (ALU_Ctrl1, not_2_out, not_5_out);
  and and_2 (and_2_out, I13, not_3_out);
  or or_2 (ALU_Src, not_4_out, not_5_out);
  or or_3 (ALU_Ctrl0, not_1_out, and_2_out);

  assign ALU_Ctrl3 = 1'b0;
endmodule

module onebit_adder (
  input  A,
  input  B,
  input  C_in,
  output S,
  output C_out
);

  wire and_1_out, and_2_out, and_3_out, and_4_out, and_5_out, and_6_out, and_7_out, not_1_out, not_2_out,
       not_3_out, not_4_out, not_5_out, not_6_out;

  not not_1 (not_1_out, A);
  not not_2 (not_2_out, B);
  and and_1 (and_1_out, not_1_out, not_2_out, C_in);
  not not_3 (not_3_out, A);
  and and_2 (and_2_out, not_3_out, B, not_4_out);
  not not_4 (not_4_out, C_in);
  not not_5 (not_5_out, B);
  and and_3 (and_3_out, A, not_5_out, not_6_out);
  not not_6 (not_6_out, C_in);
  and and_4 (and_4_out, A, B, C_in);
  and and_5 (and_5_out, B, C_in);
  and and_6 (and_6_out, A, C_in);
  and and_7 (and_7_out, A, B);
  or or_1 (S, and_1_out, and_2_out, and_3_out, and_4_out);
  or or_2 (C_out, and_5_out, and_6_out, and_7_out);
endmodule

module onebit_ALU (
  input  [3:0] ALU_Ctrl,
  input  A,
  input  B,
  input  C_in,
  output R,
  output C_out
);

  wire and_1_out, multiplexer_1_out, not_1_out, onebit_adder_1_s, or_1_out, xor_1_out;

  Multiplexer #(.enable("false")) multiplexer_1 (.in0(B), .in1(not_1_out), .out(multiplexer_1_out), .sel(ALU_Ctrl[2]));
  not not_1 (not_1_out, B);
  and and_1 (and_1_out, A, multiplexer_1_out);
  or or_1 (or_1_out, A, multiplexer_1_out);
  xor xor_1 (xor_1_out, A, multiplexer_1_out);
  onebit_adder onebit_adder_1 (.A(A), .B(multiplexer_1_out), .C_in(C_in), .S(onebit_adder_1_s), .C_out(C_out));
  Multiplexer #(.enable("false"), .select(2)) multiplexer_2 (
    .in0(and_1_out), .in1(or_1_out), .in2(xor_1_out), .in3(onebit_adder_1_s), .out(R), .sel(ALU_Ctrl[1:0]));
endmodule

module fourbit_ALU (
  input  [3:0] ALU_Ctrl,
  input  [3:0] A,
  input  [3:0] B,
  input  C_in,
  output [3:0] R,
  output C_out
);

  wire onebit_alu_1_c_out, onebit_alu_2_c_out, onebit_alu_3_c_out;

  onebit_ALU onebit_alu_1 (.ALU_Ctrl(ALU_Ctrl), .A(A[0]), .B(B[0]), .C_in(C_in), .R(R[0]), .C_out(onebit_alu_1_c_out));
  onebit_ALU onebit_alu_2 (
    .ALU_Ctrl(ALU_Ctrl), .A(A[1]), .B(B[1]), .C_in(onebit_alu_1_c_out), .R(R[1]), .C_out(onebit_alu_2_c_out));
  onebit_ALU onebit_alu_3 (
    .ALU_Ctrl(ALU_Ctrl), .A(A[2]), .B(B[2]), .C_in(onebit_alu_2_c_out), .R(R[2]), .C_out(onebit_alu_3_c_out));
  onebit_ALU onebit_alu_4 (.ALU_Ctrl(ALU_Ctrl), .A(A[3]), .B(B[3]), .C_in(onebit_alu_3_c_out), .R(R[3]), .C_out(C_out));
endmodule

module ALU_32 (
  input  [3:0] ALU_Ctrl,
  input  [31:0] A,
  input  [31:0] B,
  output [31:0] Result,
  output C_out
);

  wire fourbit_alu_1_c_out, fourbit_alu_2_c_out, fourbit_alu_3_c_out, fourbit_alu_4_c_out,
       fourbit_alu_5_c_out, fourbit_alu_6_c_out, fourbit_alu_7_c_out;

  fourbit_ALU fourbit_alu_1 (
    .ALU_Ctrl(ALU_Ctrl), .A(A[3:0]), .B(B[3:0]), .C_in(ALU_Ctrl[2]), .R(Result[3:0]),
    .C_out(fourbit_alu_1_c_out));
  fourbit_ALU fourbit_alu_2 (
    .ALU_Ctrl(ALU_Ctrl), .A(A[7:4]), .B(B[7:4]), .C_in(fourbit_alu_1_c_out), .R(Result[7:4]),
    .C_out(fourbit_alu_2_c_out));
  fourbit_ALU fourbit_alu_3 (
    .ALU_Ctrl(ALU_Ctrl), .A(A[11:8]), .B(B[11:8]), .C_in(fourbit_alu_2_c_out), .R(Result[11:8]),
    .C_out(fourbit_alu_3_c_out));
  fourbit_ALU fourbit_alu_4 (
    .ALU_Ctrl(ALU_Ctrl), .A(A[15:12]), .B(B[15:12]), .C_in(fourbit_alu_3_c_out), .R(Result[15:12]),
    .C_out(fourbit_alu_4_c_out));
  fourbit_ALU fourbit_alu_5 (
    .ALU_Ctrl(ALU_Ctrl), .A(A[19:16]), .B(B[19:16]), .C_in(fourbit_alu_4_c_out), .R(Result[19:16]),
    .C_out(fourbit_alu_5_c_out));
  fourbit_ALU fourbit_alu_6 (
    .ALU_Ctrl(ALU_Ctrl), .A(A[23:20]), .B(B[23:20]), .C_in(fourbit_alu_5_c_out), .R(Result[23:20]),
    .C_out(fourbit_alu_6_c_out));
  fourbit_ALU fourbit_alu_7 (
    .ALU_Ctrl(ALU_Ctrl), .A(A[27:24]), .B(B[27:24]), .C_in(fourbit_alu_6_c_out), .R(Result[27:24]),
    .C_out(fourbit_alu_7_c_out));
  fourbit_ALU fourbit_alu_8 (
    .ALU_Ctrl(ALU_Ctrl), .A(A[31:28]), .B(B[31:28]), .C_in(fourbit_alu_7_c_out), .R(Result[31:28]),
    .C_out(C_out));
endmodule

module reg_4_32 (
  input  [1:0] RReg1,
  input  [1:0] RReg2,
  input  [31:0] WData,
  input  Clock_in,
  input  Write,
  input  [1:0] WReg,
  output [31:0] RData1,
  output [31:0] RData2
);

  wire demultiplexer_1_out0, demultiplexer_1_out1, demultiplexer_1_out2, demultiplexer_1_out3;
  wire [31:0] register_1_q, register_2_q, register_3_q, register_4_q;

  Demultiplexer #(.enable("false"), .select(2)) demultiplexer_1 (
    .out0(demultiplexer_1_out0), .out1(demultiplexer_1_out1), .out2(demultiplexer_1_out2),
    .out3(demultiplexer_1_out3), .in(Write), .sel(WReg));
  Register #(.width(32)) register_1 (
    .D(WData), .en(demultiplexer_1_out0), .clk(Clock_in), .Q(register_1_q), .clr(Write));
  Register #(.width(32)) register_2 (
    .D(WData), .en(demultiplexer_1_out1), .clk(Clock_in), .Q(register_2_q));  // open: clr
  Register #(.width(32)) register_3 (
    .D(WData), .en(demultiplexer_1_out2), .clk(Clock_in), .Q(register_3_q));  // open: clr
  Register #(.width(32)) register_4 (
    .D(WData), .en(demultiplexer_1_out3), .clk(Clock_in), .Q(register_4_q));  // open: clr
  Multiplexer #(.enable("false"), .select(2), .width(32)) multiplexer_1 (
    .in0(register_1_q), .in1(register_2_q), .in2(register_3_q), .in3(register_4_q), .out(RData1), .sel(RReg1));
  Multiplexer #(.enable("false"), .select(2), .width(32)) multiplexer_2 (
    .in0(register_1_q), .in1(register_2_q), .in2(register_3_q), .in3(register_4_q), .out(RData2), .sel(RReg2));
endmodule

module reg_4_32_0 (
  input  [1:0] RReg1,
  input  [31:0] W_Data,
  input  [1:0] RReg2,
  input  Clock_in,
  input  Write,
  input  [1:0] WReg,
  output [31:0] RData1,
  output [31:0] RData2
);

  wire demultiplexer_1_out0, demultiplexer_1_out1, demultiplexer_1_out2, demultiplexer_1_out3;
  wire [31:0] register_1_q, register_2_q, register_3_q, register_4_q;

  Demultiplexer #(.enable("false"), .select(2)) demultiplexer_1 (
    .out0(demultiplexer_1_out0), .out1(demultiplexer_1_out1), .out2(demultiplexer_1_out2),
    .out3(demultiplexer_1_out3), .in(Write), .sel(WReg));
  Register #(.width(32)) register_1 (
    .D(W_Data), .en(demultiplexer_1_out0), .clk(Clock_in), .Q(register_1_q));  // open: clr
  Register #(.width(32)) register_2 (
    .D(W_Data), .en(demultiplexer_1_out1), .clk(Clock_in), .Q(register_2_q));  // open: clr
  Register #(.width(32)) register_3 (
    .D(W_Data), .en(demultiplexer_1_out2), .clk(Clock_in), .Q(register_3_q));  // open: clr
  Register #(.width(32)) register_4 (
    .D(W_Data), .en(demultiplexer_1_out3), .clk(Clock_in), .Q(register_4_q));  // open: clr
  Multiplexer #(.enable("false"), .select(2), .width(32)) multiplexer_1 (
    .in0(register_1_q), .in1(register_2_q), .in2(register_3_q), .in3(register_4_q), .out(RData1), .sel(RReg1));
  Multiplexer #(.enable("false"), .select(2), .width(32)) multiplexer_2 (
    .in0(register_1_q), .in1(register_2_q), .in2(register_3_q), .in3(register_4_q), .out(RData2), .sel(RReg2));
endmodule

module reg_file (
  input  [4:0] RReg_1,
  input  [4:0] RReg_2,
  input  [31:0] WData,
  input  Clock_in,
  input  Write,
  input  [4:0] W_Reg,
  output [31:0] RData_1,
  output [31:0] RData_2
);

  wire W3_0, W7_4, W11_8, W15_12, W19_16, W23_20, W27_24, W31_28;
  wire [31:0] reg_4_32_0_1_rdata1, reg_4_32_0_1_rdata2, reg_4_32_0_2_rdata1, reg_4_32_0_2_rdata2,
       reg_4_32_0_3_rdata1, reg_4_32_0_3_rdata2, reg_4_32_0_4_rdata1, reg_4_32_0_4_rdata2,
       reg_4_32_0_5_rdata1, reg_4_32_0_5_rdata2, reg_4_32_0_6_rdata1, reg_4_32_0_6_rdata2,
       reg_4_32_0_7_rdata1, reg_4_32_0_7_rdata2, reg_4_32_1_rdata1, reg_4_32_1_rdata2;

  Demultiplexer #(.enable("false"), .select(3)) demultiplexer_1 (
    .out0(W3_0), .out1(W7_4), .out2(W11_8), .out3(W15_12), .out4(W19_16), .out5(W23_20), .out6(W27_24),
    .out7(W31_28), .in(Write), .sel(W_Reg[4:2]));
  reg_4_32 reg_4_32_1 (
    .RReg1(RReg_1[1:0]), .RReg2(RReg_2[1:0]), .WData(WData), .Clock_in(Clock_in), .Write(W3_0),
    .WReg(W_Reg[1:0]), .RData1(reg_4_32_1_rdata1), .RData2(reg_4_32_1_rdata2));
  reg_4_32_0 reg_4_32_0_1 (
    .RReg1(RReg_1[1:0]), .W_Data(WData), .RReg2(RReg_2[1:0]), .Clock_in(Clock_in), .Write(W7_4),
    .WReg(W_Reg[1:0]), .RData1(reg_4_32_0_1_rdata1), .RData2(reg_4_32_0_1_rdata2));
  reg_4_32_0 reg_4_32_0_2 (
    .RReg1(RReg_1[1:0]), .W_Data(WData), .RReg2(RReg_2[1:0]), .Clock_in(Clock_in), .Write(W11_8),
    .WReg(W_Reg[1:0]), .RData1(reg_4_32_0_2_rdata1), .RData2(reg_4_32_0_2_rdata2));
  reg_4_32_0 reg_4_32_0_3 (
    .RReg1(RReg_1[1:0]), .W_Data(WData), .RReg2(RReg_2[1:0]), .Clock_in(Clock_in), .Write(W15_12),
    .WReg(W_Reg[1:0]), .RData1(reg_4_32_0_3_rdata1), .RData2(reg_4_32_0_3_rdata2));
  reg_4_32_0 reg_4_32_0_4 (
    .RReg1(RReg_1[1:0]), .W_Data(WData), .RReg2(RReg_2[1:0]), .Clock_in(Clock_in), .Write(W19_16),
    .WReg(W_Reg[1:0]), .RData1(reg_4_32_0_4_rdata1), .RData2(reg_4_32_0_4_rdata2));
  reg_4_32_0 reg_4_32_0_5 (
    .RReg1(RReg_1[1:0]), .W_Data(WData), .RReg2(RReg_2[1:0]), .Clock_in(Clock_in), .Write(W23_20),
    .WReg(W_Reg[1:0]), .RData1(reg_4_32_0_5_rdata1), .RData2(reg_4_32_0_5_rdata2));
  reg_4_32_0 reg_4_32_0_6 (
    .RReg1(RReg_1[1:0]), .W_Data(WData), .RReg2(RReg_2[1:0]), .Clock_in(Clock_in), .Write(W27_24),
    .WReg(W_Reg[1:0]), .RData1(reg_4_32_0_6_rdata1), .RData2(reg_4_32_0_6_rdata2));
  reg_4_32_0 reg_4_32_0_7 (
    .RReg1(RReg_1[1:0]), .W_Data(WData), .RReg2(RReg_2[1:0]), .Clock_in(Clock_in), .Write(W31_28),
    .WReg(W_Reg[1:0]), .RData1(reg_4_32_0_7_rdata1), .RData2(reg_4_32_0_7_rdata2));
  Multiplexer #(.enable("false"), .select(3), .width(32)) multiplexer_1 (
    .in0(reg_4_32_1_rdata1), .in1(reg_4_32_0_1_rdata1), .in2(reg_4_32_0_2_rdata1), .in3(reg_4_32_0_3_rdata1),
    .in4(reg_4_32_0_4_rdata1), .in5(reg_4_32_0_5_rdata1), .in6(reg_4_32_0_6_rdata1),
    .in7(reg_4_32_0_7_rdata1), .out(RData_1), .sel(RReg_1[4:2]));
  Multiplexer #(.enable("false"), .select(3), .width(32)) multiplexer_2 (
    .in0(reg_4_32_1_rdata2), .in1(reg_4_32_0_1_rdata2), .in2(reg_4_32_0_2_rdata2), .in3(reg_4_32_0_3_rdata2),
    .in4(reg_4_32_0_4_rdata2), .in5(reg_4_32_0_5_rdata2), .in6(reg_4_32_0_6_rdata2),
    .in7(reg_4_32_0_7_rdata2), .out(RData_2), .sel(RReg_2[4:2]));

  // Other names for the same wires on the sheet: Clock = Clock_in
endmodule

module final_product (
  input  [31:0] Instruction
);

  wire alu_control_1_alu_src, clock_1_out, undriven, undriven_2, undriven_3, undriven_4, undriven_5,
       undriven_6;
  wire [3:0] alu_control_1_alu_ctrl0;
  wire [31:0] alu_32_1_result, bit_extender_1_out, multiplexer_1_out, reg_file_1_rdata_1, reg_file_1_rdata_2;

  Clock clock_1 (.out(clock_1_out));
  assign bit_extender_1_out = {{20{Instruction[31]}}, Instruction[31:20]};  // Bit_Extender bit_extender_1
  reg_file reg_file_1 (
    .RReg_1(Instruction[19:15]), .RReg_2(Instruction[24:20]), .WData(alu_32_1_result),
    .Clock_in(clock_1_out), .Write(1'b1), .W_Reg(Instruction[11:7]), .RData_1(reg_file_1_rdata_1),
    .RData_2(reg_file_1_rdata_2));
  ALU_control alu_control_1 (
    .I30(undriven), .I14(undriven_2), .I13(undriven_3), .I12(undriven_4), .I6(undriven_5), .I5(undriven_6),
    .I4(Instruction[4]), .ALU_Ctrl3(alu_control_1_alu_ctrl0[3]), .ALU_Ctrl2(alu_control_1_alu_ctrl0[2]),
    .ALU_Ctrl1(alu_control_1_alu_ctrl0[1]), .ALU_Ctrl0(alu_control_1_alu_ctrl0[0]),
    .ALU_Src(alu_control_1_alu_src));
  Multiplexer #(.enable("false"), .width(32)) multiplexer_1 (
    .in0(reg_file_1_rdata_2), .in1(bit_extender_1_out), .out(multiplexer_1_out), .sel(alu_control_1_alu_src));
  ALU_32 alu_32_1 (
    .ALU_Ctrl(alu_control_1_alu_ctrl0), .A(reg_file_1_rdata_1), .B(multiplexer_1_out),
    .Result(alu_32_1_result));  // open: C_out
endmodule
